# Fritzing sketch Untitled Sketch (saved by Fritzing 0.9.3b)

parts:
  KY-1 = Keyes Relay [package=THT]
  KY-2 = Keyes Relay [package=THT]
  WeMos_D1_Mini1 = WeMos D1 Mini
  AC_Power = Dagu DGServo 9g header (male) [package=THT]
  Motor_Blue = Inductor [package="400 mil [THT]"]
  Motor_Black = Inductor [package="400 mil [THT]"]
  Motor_Brown = Inductor [package="400 mil [THT]"]
  Motor_Green = Inductor [package="400 mil [THT]"]

nets:
  N1: KY-1.signal, WeMos_D1_Mini1.D1
  N2: KY-1.power, KY-2.power, WeMos_D1_Mini1.5V
  N3: KY-1.ground, KY-2.ground, WeMos_D1_Mini1.G
  N4: KY-1.C, KY-2.C, AC_Power.gnd
  N5: KY-1.NO, Motor_Black.pin_0
  N6: KY-2.signal, WeMos_D1_Mini1.D2
  N7: KY-2.NO, Motor_Brown.pin_0
  N8: AC_Power.Vcc, Motor_Blue.pin_0
  N9: AC_Power.pulse, Motor_Green.pin_0

custom parts:
  Keyes Relay: The Keyes 5V relay module is suitable for SCM development, home appliance control. It uses a 5V~12V TIL control signal which can control DC / AC signal.
